// Logisim project Seletor.circ as structural Verilog: 1 circuit, main circuit main
module main (
);

  wire button_1_out, button_2_out, button_3_out, button_4_out, nand_1_out, nand_2_out, nand_3_out,
       nand_4_out, not_1_out, not_2_out;

  Button button_1 (.out(button_1_out));
  Button button_2 (.out(button_2_out));
  Button button_3 (.out(button_3_out));
  Button button_4 (.out(button_4_out));
  not not_1 (not_1_out, button_2_out);
  nand nand_1 (nand_1_out, button_1_out, button_2_out);
  nand nand_2 (nand_2_out, not_1_out, button_3_out);
  nand nand_3 (nand_3_out, nand_1_out, nand_2_out);
  not not_2 (not_2_out, button_4_out);
  nand nand_4 (nand_4_out, nand_3_out, not_2_out);
  LED led_1 (.in(nand_4_out));

  // Notes on the sheet:
  //   Clock A
  //   Select
  //   Clock B
  //   Halt
endmodule
