// Logisim project Esquema.circ as structural Verilog: 3 circuits, main circuit main
module main (
);

  wire _74LS161_out_9, _74LS161_out_10, _74LS245_out_13, A, B, C, Clock_out, D, Jump_out, PC_Inc_out,
       PC_Out_out, pull_resistor_1_node, pull_resistor_2_node, pull_resistor_3_node, pull_resistor_4_node,
       Reset_out, undriven_2, undriven_3, undriven_4, undriven_5;
  wire [3:0] undriven;

  Button PC_Inc (.out(PC_Inc_out));
  Button Reset (.out(Reset_out));
  Button PC_Out (.out(PC_Out_out));
  Button Clock (.out(Clock_out));
  Button Jump (.out(Jump_out));
  _74LS161 _74LS161 (
    .in_1(Reset_out), .in_2(Clock_out), .in_3(undriven[0]), .in_4(undriven[1]), .in_5(undriven[2]),
    .in_6(undriven[3]), .in_7(PC_Inc_out), .in_8(1'b0), .out_9(_74LS161_out_9), .out_10(_74LS161_out_10),
    .out_11(A), .out_12(B), .out_13(C), .out_14(D), .out_15(PC_Inc_out), .out_16(Jump_out));
  LED led_1 (.in(A));
  LED led_2 (.in(D));
  LED led_3 (.in(C));
  LED led_4 (.in(B));
  Pull_Resistor pull_resistor_1 (.node(pull_resistor_1_node));
  Pull_Resistor pull_resistor_2 (.node(pull_resistor_2_node));
  Pull_Resistor pull_resistor_3 (.node(pull_resistor_3_node));
  Pull_Resistor pull_resistor_4 (.node(pull_resistor_4_node));
  _74LS245 _74LS245 (
    .in_1(_74LS245_out_13), .in_2(undriven_2), .in_3(undriven_3), .in_4(undriven_4), .in_5(undriven_5),
    .in_6(undriven[0]), .in_7(undriven[1]), .in_8(undriven[2]), .in_9(undriven[3]), .in_10(_74LS245_out_13),
    .out_11(_74LS161_out_9), .out_12(PC_Out_out), .out_13(_74LS245_out_13), .out_14(_74LS245_out_13),
    .out_15(_74LS245_out_13), .out_16(_74LS245_out_13), .out_17(D), .out_18(C), .out_19(B), .out_20(A));
  // also tied to GND on the sheet: _74LS245_out_13
  // also tied to VCC on the sheet: _74LS161_out_9
endmodule

module _74LS161 (
  input  in_1,
  input  in_2,
  input  in_3,
  input  in_4,
  input  in_5,
  input  in_6,
  input  in_7,
  input  in_8,
  output out_9,
  output out_10,
  output out_11,
  output out_12,
  output out_13,
  output out_14,
  output out_15,
  output out_16
);
endmodule

module _74LS245 (
  input  in_1,
  input  in_2,
  input  in_3,
  input  in_4,
  input  in_5,
  input  in_6,
  input  in_7,
  input  in_8,
  input  in_9,
  input  in_10,
  output out_11,
  output out_12,
  output out_13,
  output out_14,
  output out_15,
  output out_16,
  output out_17,
  output out_18,
  output out_19,
  output out_20
);
endmodule
